# Fritzing sketch Dfplayer (saved by Fritzing 0.9.3b)
breadboards: 1

parts:
  Componente1 = Arduino Mega 2560 (Rev3)
  DFRobot_DFPlayer_Mini1 = DFRobot DFPlayer Mini [part_number=DFR0299]
  R1 = Resistor [tolerance=±5% resistance=220 package="0603 [SMD]"]
  SP1 = SPEAKER [package=pcb_mount_speaker]
  R2 = Resistor [tolerance=±5% resistance=220 package="0603 [SMD]"]

nets:
  N1: Componente1.D19/RX1, R2.Pin_0
  N2: Componente1.D18/TX1, R1.Pin_0
  N3: Componente1.GND, DFRobot_DFPlayer_Mini1.GND-1, DFRobot_DFPlayer_Mini1.GND-2
  5V: Componente1.5V, DFRobot_DFPlayer_Mini1.VCC
  N4: DFRobot_DFPlayer_Mini1.RX, R2.Pin_1
  N5: DFRobot_DFPlayer_Mini1.TX, R1.Pin_1
  N6: DFRobot_DFPlayer_Mini1.SPK_1, SP1.-
  N7: DFRobot_DFPlayer_Mini1.SPK_2, SP1.+

notes:
  1 K
